# Fritzing sketch Give Sign Circuit (saved by Fritzing 0.9.0b)
breadboards: 1

parts:
  Part1 = Spark Core (v1.0)
  12V/5A_DC_Power_Supply_2_1mm_Jack = Power plug
  7805_Voltage_Reg = Voltage Regulator [package=78xxl]
  10uf = Capacitor Polarized [package=cpol-radial-10uf-25v]
  10uf_2 = Capacitor Polarized [package=cpol-radial-10uf-25v]
  Power_LED = smd LED [color="Green (560nm)" package="0805 [SMD]"]
  R1 = Resistor [package="2512 [SMD]"]
  J1 = Screw terminal - 2 pins [package=THT]
  J2 = Screw terminal - 2 pins [package=THT]

nets:
  N1: Part1.A3, J2.pin1
  N2: Part1.A5, J2.pin2
  GND: Part1.GND, 12V/5A_DC_Power_Supply_2_1mm_Jack.GND, Power_LED.cathode, J1.pin2
  N3: Part1.VIN, 7805_Voltage_Reg.OUT, 10uf_2.+, R1.Pin_0
  N4: 12V/5A_DC_Power_Supply_2_1mm_Jack.VCC, 7805_Voltage_Reg.IN, 10uf.+, J1.pin1
  N5: 7805_Voltage_Reg.GND, 10uf.-, 10uf_2.-

notes:
  To LED Strips
